// Logisim project A.circ as structural Verilog: 1 circuit, main circuit main
module main (
  input  x,
  input  y
);

  wire xnor_1_out, xnor_2_out, xor_1_out, xor_2_out, xor_3_out;

  xnor xnor_1 (xnor_1_out, x, y);
  xor xor_1 (xor_1_out, x, xnor_1_out);
  xor xor_2 (xor_2_out, xnor_1_out, y);
  xnor xnor_2 (xnor_2_out, xor_1_out, xor_2_out);
  xor xor_3 (xor_3_out, xnor_2_out, xnor_2_out);
  // Probe on nothing
endmodule
