// Logisim project B.circ as structural Verilog: 1 circuit, main circuit main
module main (
  input  x,
  input  y,
  output f
);

  wire n747266_1_pin8, n747266_1_pin9, n747266_1_pin10, n747266_1_pin11;

  _747266 u_747266_1 (
    .pin13(x), .pin12(y), .pin11(n747266_1_pin11), .pin10(n747266_1_pin10), .pin9(n747266_1_pin9),
    .pin8(n747266_1_pin8));  // open: pin1, pin2, pin3, pin4, pin5, pin6
  _7486 u_7486_1 (
    .pin1(n747266_1_pin8), .pin2(n747266_1_pin8), .pin3(f), .pin13(x), .pin12(n747266_1_pin11),
    .pin11(n747266_1_pin10), .pin10(y), .pin9(n747266_1_pin11), .pin8(n747266_1_pin9));  // open: pin4, pin5, pin6
endmodule
